// Logisim project compute_of_8bit.circ as structural Verilog: 7 circuits, main circuit AU
module AU (
  input  CRT,
  input  [7:0] IN_A,
  input  [7:0] IN_B,
  output [7:0] OUT
);

  wire [7:0] adder_1_out, multiplexer_1_out, not_1_out;

  assign not_1_out = ~IN_B;  // NOT_Gate not_1, 8 bits wide
  Adder adder_1 (.a(not_1_out), .b(8'h1), .out(adder_1_out));  // open: cin, cout
  Multiplexer #(.width(8), .enable("false")) multiplexer_1 (
    .in0(adder_1_out), .in1(IN_B), .out(multiplexer_1_out), .sel(CRT));
  Adder adder_2 (.a(IN_A), .b(multiplexer_1_out), .out(OUT));  // open: cin, cout
endmodule

module LU (
  input  CRT,
  input  [7:0] IN_A,
  input  [7:0] IN_B,
  output [7:0] OUT
);

  wire [7:0] and_1_out, or_1_out;

  assign and_1_out = IN_A & IN_B;  // AND_Gate and_1, 8 bits wide
  assign or_1_out = IN_B | IN_A;  // OR_Gate or_1, 8 bits wide
  Multiplexer #(.width(8), .enable("false")) multiplexer_1 (.in0(and_1_out), .in1(or_1_out), .out(OUT), .sel(CRT));
endmodule

module ALU (
  input  [5:0] CRT,
  input  [7:0] IN_A,
  input  [7:0] IN_B,
  output [7:0] OUT
);

  wire [7:0] and_1_out, and_2_out, au_1_out, lu_1_out, multiplexer_1_out, not_1_out, or_1_out;

  assign or_1_out = IN_A | IN_B;  // OR_Gate or_1, 8 bits wide
  assign and_1_out = IN_A & IN_B;  // AND_Gate and_1, 8 bits wide
  LU lu_1 (.CRT(CRT[3]), .IN_A(IN_A), .IN_B(IN_B), .OUT(lu_1_out));
  AU au_1 (.CRT(CRT[2]), .IN_A(IN_A), .IN_B(IN_B), .OUT(au_1_out));
  assign and_2_out = or_1_out & and_1_out;  // AND_Gate and_2, 8 bits wide
  Multiplexer #(.width(8), .enable("false")) multiplexer_1 (
    .in0(lu_1_out), .in1(au_1_out), .out(multiplexer_1_out), .sel(CRT[1]));
  assign not_1_out = ~and_2_out;  // NOT_Gate not_1, 8 bits wide
  Multiplexer #(.width(8), .enable("false")) multiplexer_2 (
    .in0(multiplexer_1_out), .in1(not_1_out), .out(OUT), .sel(CRT[0]));

  // Notes on the sheet:
  //   Judge ==
endmodule

module RegisterGroup (
  input  [4:0] READ_ADDR,
  input  [4:0] READ_ADDR2,
  input  [7:0] DATA_IN,
  input  [4:0] WRITE_ADDR,
  input  WRITE_EN,
  input  CLK,
  input  Clear,
  output [7:0] OUT_1,
  output [7:0] OUT_2,
  output [7:0] IO_5,
  output [7:0] IO_6
);

  wire and_1_out, and_2_out, and_3_out, and_4_out, and_5_out, and_6_out, and_7_out, decoder_1_out0,
       decoder_1_out1, decoder_1_out2, decoder_1_out3, decoder_1_out4, decoder_1_out5, decoder_1_out6,
       decoder_1_out7, undriven;
  wire [7:0] register_1_q, register_2_q, register_3_q, register_4_q, register_5_q, register_8_q;

  Decoder #(.select(3), .enable("false")) decoder_1 (
    .out0(decoder_1_out0), .out1(decoder_1_out1), .out2(decoder_1_out2), .out3(decoder_1_out3),
    .out4(decoder_1_out4), .out5(decoder_1_out5), .out6(decoder_1_out6), .out7(decoder_1_out7),
    .sel(WRITE_ADDR[2:0]));
  and and_1 (and_1_out, decoder_1_out0, WRITE_EN);
  and and_2 (and_2_out, decoder_1_out1, WRITE_EN);
  and and_3 (and_3_out, decoder_1_out2, WRITE_EN);
  and and_4 (and_4_out, decoder_1_out3, WRITE_EN);
  and and_5 (and_5_out, decoder_1_out4, WRITE_EN);
  and and_6 (and_6_out, decoder_1_out5, WRITE_EN);
  and and_7 (and_7_out, decoder_1_out6, WRITE_EN);
  // AND_Gate and_8 has open pins: in0=decoder_1_out7, in1=WRITE_EN, out=open
  Register register_1 (.D(DATA_IN), .en(and_1_out), .Q(register_1_q), .clk(CLK), .clr(Clear));
  Register register_2 (.D(DATA_IN), .en(and_2_out), .Q(register_2_q), .clk(CLK), .clr(Clear));
  Register register_3 (.D(DATA_IN), .en(and_3_out), .Q(register_3_q), .clk(CLK), .clr(Clear));
  Register register_4 (.D(DATA_IN), .en(and_4_out), .Q(register_4_q), .clk(CLK), .clr(Clear));
  Register register_5 (.D(DATA_IN), .en(and_5_out), .Q(register_5_q), .clk(CLK), .clr(Clear));
  Register register_6 (.D(DATA_IN), .en(and_6_out), .Q(IO_5), .clk(CLK), .clr(Clear));
  Register register_7 (.D(DATA_IN), .en(and_7_out), .Q(IO_6), .clk(CLK), .clr(Clear));
  Register register_8 (.en(undriven), .Q(register_8_q), .clk(undriven), .clr(1'b1));  // open: D
  Multiplexer #(.select(3), .width(8), .enable("false")) multiplexer_1 (
    .in0(register_1_q), .in1(register_2_q), .in2(register_3_q), .in3(register_4_q), .in4(register_5_q),
    .in5(IO_5), .in6(IO_6), .in7(register_8_q), .out(OUT_1), .sel(READ_ADDR[2:0]));
  Multiplexer #(.select(3), .width(8), .enable("false")) multiplexer_2 (
    .in0(register_1_q), .in1(register_2_q), .in2(register_3_q), .in3(register_4_q), .in4(register_5_q),
    .in5(IO_5), .in6(IO_6), .in7(register_8_q), .out(OUT_2), .sel(READ_ADDR2[2:0]));
endmodule

module CPU (
  input  CLK,
  input  [7:0] RAMDataIn,
  input  [31:0] CodeIn,
  input  CLEAR,
  output [7:0] out_5,
  output [7:0] RAMAddr,
  output [7:0] RAMDataOut,
  output RAM_Read_Write,
  output [7:0] IO_6,
  output [7:0] IO_5
);

  wire [7:0] bit_extender_1_out, bit_extender_2_out, multiplexer_1_out, multiplexer_2_out, multiplexer_3_out,
       registergroup_1_out_1;

  PC pc_1 (.OUT(out_5), .JumpPos(bit_extender_1_out), .JumpEn(CodeIn[28]), .CLEAR(CLEAR), .CLK(CLK));
  Bit_Extender #(.in_width(32), .out_width(8)) bit_extender_1 (.in(CodeIn), .out(bit_extender_1_out));
  Bit_Extender #(.in_width(10), .out_width(8)) bit_extender_2 (.in(CodeIn[15:6]), .out(bit_extender_2_out));
  Multiplexer #(.width(8), .enable("false")) multiplexer_1 (
    .in0(RAMAddr), .in1(RAMDataIn), .out(multiplexer_1_out), .sel(CodeIn[30]));
  RegisterGroup registergroup_1 (
    .READ_ADDR(CodeIn[25:21]), .READ_ADDR2(CodeIn[20:16]), .DATA_IN(multiplexer_1_out),
    .WRITE_ADDR(CodeIn[20:16]), .OUT_1(registergroup_1_out_1), .OUT_2(RAMDataOut), .IO_5(IO_5), .IO_6(IO_6),
    .WRITE_EN(CodeIn[31]), .CLK(CLK), .Clear(CLEAR));
  Multiplexer #(.width(8), .enable("false")) multiplexer_2 (
    .in0(registergroup_1_out_1), .in1(IO_5), .out(multiplexer_2_out), .sel(CodeIn[4]));
  Multiplexer #(.width(8), .enable("false")) multiplexer_3 (
    .in0(bit_extender_2_out), .in1(IO_6), .out(multiplexer_3_out), .sel(CodeIn[4]));
  ALU alu_1 (.CRT(CodeIn[5:0]), .IN_A(multiplexer_2_out), .IN_B(multiplexer_3_out), .OUT(RAMAddr));

  assign RAM_Read_Write = CodeIn[29];

  // Notes on the sheet:
  //   CodeLoc
endmodule

module PC (
  input  JumpEn,
  input  [7:0] JumpPos,
  input  CLK,
  input  CLEAR,
  output [7:0] OUT
);

  wire [7:0] multiplexer_1_out, register_1_q;

  Multiplexer #(.width(8), .enable("false")) multiplexer_1 (
    .in0(OUT), .in1(JumpPos), .out(multiplexer_1_out), .sel(JumpEn));
  Register register_1 (.D(multiplexer_1_out), .Q(register_1_q), .clk(CLK), .clr(CLEAR));  // open: en
  Adder adder_1 (.a(register_1_q), .b(8'h1), .out(OUT));  // open: cin, cout
endmodule

module Computer (
);

  wire clock_1_out, cpu_1_ram_read_write, not_1_out;
  wire [7:0] cpu_1_io_5, cpu_1_io_6, cpu_1_out_5, cpu_1_ramaddr, cpu_1_ramdataout, ram_1_data;
  wire [31:0] rom_1_data;

  ROM #(.dataWidth(32)) rom_1 (.addr(cpu_1_out_5), .data(rom_1_data));  // open: sel
  CPU cpu_1 (
    .out_5(cpu_1_out_5), .CodeIn(rom_1_data), .RAMDataIn(ram_1_data), .RAMAddr(cpu_1_ramaddr),
    .RAMDataOut(cpu_1_ramdataout), .RAM_Read_Write(cpu_1_ram_read_write), .CLK(clock_1_out),
    .IO_6(cpu_1_io_6), .IO_5(cpu_1_io_5));  // open: CLEAR
  // DotMatrix #(.inputtype("select"), .matrixcols(8), .matrixrows(8)) dotmatrix_1: pin names not known; wires that end beside it: cpu_1_io_5, cpu_1_io_6
  Clock clock_1 (.out(clock_1_out));
  not not_1 (not_1_out, cpu_1_ram_read_write);
  RAM #(.bus("separate")) ram_1 (
    .addr(cpu_1_ramaddr), .din(cpu_1_ramdataout), .data(ram_1_data), .str(cpu_1_ram_read_write),
    .clk(clock_1_out), .ld(not_1_out));  // open: sel, clr

  // Notes on the sheet:
  //   ROM
  //   contents of rom_1 (hex, n*v repeats v):
  //   0 84e50046 84e60046 84e50086 84e500c6 84e60086 84e50106 84e60106 84e50246 84e600c6 84e60246 84e51906
  //   84e61906 84e61206 84e51206 84e60686 84e50f86 84e50846 84e61086 10000001
  //   RAM
endmodule
